# Fritzing sketch 218208772_SIT210-10.1DHD (saved by Fritzing 0.9.4)
circuit board: 8.53488cm x 5.63626cm
breadboards: 1

parts:
  Raspberry_Pi = Raspberry Pi 3 [part_number=RPI-3-V1.2]
  R1 = Resistor [tolerance=±5% resistance=220 package="0805 [SMD]"]
  LED = LEDs [package=led-1206]
  Pad2 = Pad [width=1 height=1 connect=center]
  Pad1 = Pad [width=1 height=1 connect=center]
  Pad4 = Pad [width=1 height=1 connect=center]
  Pad5 = Pad [width=1 height=1 connect=center]
  HC-SR04_Distance_Sensor = HC-SR04 Ultrasonic Distance Sensor  # not connected

nets:
  N1: Raspberry_Pi.GND, R1.Pin_0, R1.Pin_1, LED.C, Pad4.pad
  N2: Raspberry_Pi.GPIO17, Pad5.pad
  N3: Raspberry_Pi.GPIO27, Pad2.pad
  N4: Raspberry_Pi.GPIO26, LED.A
  N5: Raspberry_Pi.5V, Pad1.pad

notes:
  HC-SR04 Distance Sensor Shield
  Vcc
  Trig
  Echo
  Gnd
